// Digital circuit CPU.dig as structural Verilog
module CPU (
  input  [7:0] value,
  input  [1:0] dest,
  input  [1:0] src,
  input  tworeg,
  output [31:0] r0,
  output [31:0] r1,
  output [31:0] r2,
  output [31:0] r3,
  output [1:0] rd,
  output [1:0] rd_2,
  output [31:0] L,
  output [1:0] rs,
  output [31:0] target,
  output [3:0] PC,
  output [31:0] R,
  output [1:0] rd_3,
  output [1:0] rs_2,
  output [31:0] R_2
);

  wire add, add_out, Advance_out, assembler_1_p10, assembler_1_p11, decoder_1_p1, decoder_1_p2,
       decoder_1_p11, execute_1_p4, fecthc_counter_1_p7, hexdisplay_1_p1, hexdisplay_1_p2, hexdisplay_1_p3,
       hexdisplay_1_p4, hexdisplay_1_p5, hexdisplay_1_p6, hexdisplay_1_p7, hexdisplay_1_p8, hexdisplay_2_p1,
       hexdisplay_2_p2, hexdisplay_2_p3, hexdisplay_2_p4, hexdisplay_2_p5, hexdisplay_2_p6, hexdisplay_2_p7,
       hexdisplay_2_p8, instdisplay_1_p1, instdisplay_1_p2, instdisplay_1_p3, instdisplay_1_p4,
       instdisplay_1_p5, instdisplay_1_p6, jump, jump_out, mode_out, move, move_out, not_1_out, pm_1_p6,
       pm_1_p7, pm_1_p8, regdisplay_1_p1, regdisplay_1_p2, regdisplay_2_p1, regdisplay_2_p2, tworeg_t;
  wire [2:0] op;
  wire [3:0] hexdisplay_1_d1, hexdisplay_1_d2, hexdisplay_1_d3, hexdisplay_1_d4, hexdisplay_1_d5,
       hexdisplay_1_d6, hexdisplay_1_d7, hexdisplay_1_d8, hexdisplay_2_d1, hexdisplay_2_d2, hexdisplay_2_d3,
       hexdisplay_2_d4, hexdisplay_2_d5, hexdisplay_2_d6, hexdisplay_2_d7, hexdisplay_2_d8, pm_1_p4;
  wire [15:0] instdisplay_1_d1, instdisplay_1_d2, instdisplay_1_d3, instdisplay_1_d4, instdisplay_1_d5,
       instdisplay_1_d6, pm_1_p5, PROGRAM_d, regdisplay_1_d1, regdisplay_1_d2, regdisplay_2_d1,
       regdisplay_2_d2;

  SixteenSeg sixteenseg_1 (.led(regdisplay_1_d1), .dp(regdisplay_1_p1));
  REGDISPLAY regdisplay_1 (
    .D1(regdisplay_1_d1), .P1(regdisplay_1_p1), .D2(regdisplay_1_d2), .P2(regdisplay_1_p2), .E(1'b1),
    .J(jump), .R(rd));
  SixteenSeg sixteenseg_2 (.led(regdisplay_1_d2), .dp(regdisplay_1_p2));
  Seven_Seg_Hex seven_seg_hex_1 (.d(hexdisplay_1_d1), .dp(hexdisplay_1_p1));
  not not_1 (not_1_out, jump);
  hexdisplay hexdisplay_1 (
    .D1(hexdisplay_1_d1), .P1(hexdisplay_1_p1), .D2(hexdisplay_1_d2), .P2(hexdisplay_1_p2),
    .D3(hexdisplay_1_d3), .P3(hexdisplay_1_p3), .D4(hexdisplay_1_d4), .P4(hexdisplay_1_p4),
    .D5(hexdisplay_1_d5), .P5(hexdisplay_1_p5), .D6(hexdisplay_1_d6), .P6(hexdisplay_1_p6),
    .D7(hexdisplay_1_d7), .P7(hexdisplay_1_p7), .D8(hexdisplay_1_d8), .P8(hexdisplay_1_p8), .E(not_1_out),
    .V(L));
  Seven_Seg_Hex seven_seg_hex_2 (.d(hexdisplay_1_d2), .dp(hexdisplay_1_p2));
  Seven_Seg_Hex seven_seg_hex_3 (.d(hexdisplay_1_d3), .dp(hexdisplay_1_p3));
  LED programming (.in(mode_out));
  DipSwitch mode (.out(mode_out));
  Button u_add (.out(add_out));
  Button u_move (.out(move_out));
  Button u_jump (.out(jump_out));
  Seven_Seg_Hex seven_seg_hex_4 (.d(hexdisplay_1_d4), .dp(hexdisplay_1_p4));
  Seven_Seg_Hex seven_seg_hex_5 (.d(hexdisplay_1_d5), .dp(hexdisplay_1_p5));
  // assembler assembler_1: pin names not known; wires that end beside it: jump_out, mode_out, value, dest, src, tworeg, add_out, move_out, jump_out, assembler_1_p10, assembler_1_p11
  Seven_Seg_Hex seven_seg_hex_6 (.d(hexdisplay_1_d6), .dp(hexdisplay_1_p6));
  Seven_Seg_Hex seven_seg_hex_7 (.d(hexdisplay_1_d7), .dp(hexdisplay_1_p7));
  Seven_Seg_Hex seven_seg_hex_8 (.d(hexdisplay_1_d8), .dp(hexdisplay_1_p8));
  // PM pm_1: pin names not known; wires that end beside it: assembler_1_p10, assembler_1_p11, PC, pm_1_p4, pm_1_p5, pm_1_p6, pm_1_p7, pm_1_p8
  EEPROMDualPort #(.AddrBits(4), .isProgramMemory("true"), .Bits(16)) PROGRAM (
    .A(pm_1_p4), .Din(pm_1_p5), .str(pm_1_p6), .C(pm_1_p7), .ld(pm_1_p8), .D(PROGRAM_d));
  SixteenSeg sixteenseg_3 (.led(instdisplay_1_d1), .dp(instdisplay_1_p1));
  SixteenSeg sixteenseg_4 (.led(instdisplay_1_d2), .dp(instdisplay_1_p2));
  instdisplay instdisplay_1 (
    .D1(instdisplay_1_d1), .P1(instdisplay_1_p1), .D2(instdisplay_1_d2), .P2(instdisplay_1_p2),
    .D3(instdisplay_1_d3), .P3(instdisplay_1_p3), .D4(instdisplay_1_d4), .P4(instdisplay_1_p4),
    .D5(instdisplay_1_d5), .P5(instdisplay_1_p5), .D6(instdisplay_1_d6), .P6(instdisplay_1_p6), .i(op));
  SixteenSeg sixteenseg_5 (.led(instdisplay_1_d3), .dp(instdisplay_1_p3));
  SixteenSeg sixteenseg_6 (.led(instdisplay_1_d4), .dp(instdisplay_1_p4));
  Button Advance (.out(Advance_out));
  SixteenSeg sixteenseg_7 (.led(instdisplay_1_d5), .dp(instdisplay_1_p5));
  SixteenSeg sixteenseg_8 (.led(instdisplay_1_d6), .dp(instdisplay_1_p6));
  // fecthc_counter fecthc_counter_1: pin names not known; wires that end beside it: mode_out, assembler_1_p10, PROGRAM_d, Advance_out, R, jump, fecthc_counter_1_p7, PC
  Seven_Seg_Hex seven_seg_hex_9 (.d(hexdisplay_2_d1), .dp(hexdisplay_2_p1));
  Seven_Seg_Hex seven_seg_hex_10 (.d(hexdisplay_2_d2), .dp(hexdisplay_2_p2));
  Seven_Seg_Hex seven_seg_hex_11 (.d(hexdisplay_2_d3), .dp(hexdisplay_2_p3));
  hexdisplay hexdisplay_2 (
    .D1(hexdisplay_2_d1), .P1(hexdisplay_2_p1), .D2(hexdisplay_2_d2), .P2(hexdisplay_2_p2),
    .D3(hexdisplay_2_d3), .P3(hexdisplay_2_p3), .D4(hexdisplay_2_d4), .P4(hexdisplay_2_p4),
    .D5(hexdisplay_2_d5), .P5(hexdisplay_2_p5), .D6(hexdisplay_2_d6), .P6(hexdisplay_2_p6),
    .D7(hexdisplay_2_d7), .P7(hexdisplay_2_p7), .D8(hexdisplay_2_d8), .P8(hexdisplay_2_p8), .E(1'b1), .V(R));
  // decoder decoder_1: pin names not known; wires that end beside it: decoder_1_p1, decoder_1_p2, fecthc_counter_1_p7, rs, rd, L, R, add, jump, move, decoder_1_p11, op, tworeg_t
  Seven_Seg_Hex seven_seg_hex_12 (.d(hexdisplay_2_d4), .dp(hexdisplay_2_p4));
  Seven_Seg_Hex seven_seg_hex_13 (.d(hexdisplay_2_d5), .dp(hexdisplay_2_p5));
  Seven_Seg_Hex seven_seg_hex_14 (.d(hexdisplay_2_d6), .dp(hexdisplay_2_p6));
  Seven_Seg_Hex seven_seg_hex_15 (.d(hexdisplay_2_d7), .dp(hexdisplay_2_p7));
  Seven_Seg_Hex seven_seg_hex_16 (.d(hexdisplay_2_d8), .dp(hexdisplay_2_p8));
  SixteenSeg sixteenseg_9 (.led(regdisplay_2_d1), .dp(regdisplay_2_p1));
  SixteenSeg sixteenseg_10 (.led(regdisplay_2_d2), .dp(regdisplay_2_p2));
  REGDISPLAY regdisplay_2 (
    .D1(regdisplay_2_d1), .P1(regdisplay_2_p1), .D2(regdisplay_2_d2), .P2(regdisplay_2_p2), .E(tworeg_t),
    .J(1'b0), .R(rs));
  // execute execute_1: pin names not known; wires that end beside it: L, R, decoder_1_p11, execute_1_p4
  // reg_file reg_file_1: pin names not known; wires that end beside it: rs, rd, execute_1_p4, Advance_out, decoder_1_p1, decoder_1_p2, r0, r1, r2, r3
  LED led_1 (.in(jump));
  LED led_2 (.in(add));
  LED led_3 (.in(move));

  assign R_2 = R;
  assign rd_2 = rd;
  assign rd_3 = rd;
  assign rs_2 = rs;
  assign target = R;

  // Notes on the sheet:
  //   value: default 1
  //   dest: default 1
  //   src: default 1
  //   tworeg: default 1
  //   0. R2=R2+1
  //   1. R2=R1+R2
  //   2. R3=R2
  //   3. R1=R1+R2
  //   4. R3=R1
  //   5. JUMP 1
  //   contents of PROGRAM (hex, n*v repeats v):
  //   120,61,bd,91,7d,10e
  //   jump
  //   add
  //   move
  //   R
  //   pc =
  //   =
  //   (R               )
  //   +
endmodule
