// Digital circuit decoder.dig as structural Verilog
module decoder (
  input  [31:0] rsval,
  input  [31:0] rdval,
  input  [15:0] inst,
  output [1:0] rs,
  output [1:0] rd,
  output [31:0] L,
  output [31:0] R,
  output add,
  output jump,
  output move,
  output [1:0] result_mux,
  output [2:0] op,
  output tworeg
);

  wire [31:0] bitextender_1_out;

  BitExtender #(.outputBits(32)) bitextender_1 (.in(inst[15:8]), .out(bitextender_1_out));
  Multiplexer #(.Bits(32)) multiplexer_1 (.sel(inst[0]), .in_0(bitextender_1_out), .in_1(rsval), .out(R));
  Decoder #(.Selector_Bits(3)) decoder_1 (
    .sel(inst[3:1]), .out_0(add), .out_6(move), .out_7(jump));  // open: out_1, out_2, out_3, out_4, out_5
  PriorityEncoder #(.Selector_Bits(2)) priorityencoder_1 (
    .in0(jump), .in1(add), .in2(move), .in3(1'b0), .num(result_mux));  // open: any

  assign L = rdval;
  assign op = inst[3:1];
  assign rd = inst[5:4];
  assign rs = inst[7:6];
  assign tworeg = inst[0];
endmodule
