// Digital circuit execute.dig as structural Verilog
module execute (
  input  [31:0] L,
  input  [31:0] R,
  input  [2:0] op,
  output [31:0] result,
  output halt,
  output error
);

  wire musteq, musteq_eq, not_1_out;
  wire [31:0] Add_s;

  Decoder #(.Selector_Bits(3)) decoder_1 (
    .sel(op), .out_5(musteq));  // open: out_0, out_1, out_2, out_3, out_4, out_6, out_7
  Comparator #(.Bits(32)) u_musteq (.a(L), .b(R), .eq(musteq_eq));  // open: gt, lt
  Add #(.Bits(32)) Add (.a(L), .b(R), .c_i(1'b0), .s(Add_s));  // open: c_o
  not not_1 (not_1_out, musteq_eq);
  Multiplexer #(.Selector_Bits(3), .Bits(32)) multiplexer_1 (
    .sel(op), .in_0(Add_s), .in_1({32{1'b0}}), .in_2({32{1'b0}}), .in_3({32{1'b0}}), .in_4({32{1'b0}}),
    .in_5(L), .in_6(R), .in_7(L), .out(result));
  and and_1 (halt, musteq_eq, musteq);
  and and_2 (error, musteq, not_1_out);

  // Notes on the sheet:
  //   L: default 1
  //   R: default 2
endmodule
