// Digital circuit hexdisplay.dig as structural Verilog
module hexdisplay (
  input  E,
  input  [31:0] V,
  output [3:0] D1,
  output [3:0] D2,
  output [3:0] D3,
  output [3:0] D4,
  output [3:0] D5,
  output [3:0] D6,
  output P1,
  output P2,
  output P3,
  output P4,
  output P5,
  output P6,
  output [3:0] D7,
  output P7,
  output [3:0] D8,
  output P8
);

  assign D1 = E ? V[31:28] : 4'bz;  // Driver driver_1
  assign D2 = E ? V[27:24] : 4'bz;  // Driver driver_2
  assign D3 = E ? V[23:20] : 4'bz;  // Driver driver_3
  assign D4 = E ? V[19:16] : 4'bz;  // Driver driver_4
  assign D5 = E ? V[15:12] : 4'bz;  // Driver driver_5
  assign D6 = E ? V[11:8] : 4'bz;  // Driver driver_6
  assign D7 = E ? V[7:4] : 4'bz;  // Driver driver_7
  assign D8 = E ? V[3:0] : 4'bz;  // Driver driver_8

  assign P1 = 1'b0;
  assign P2 = 1'b0;
  assign P3 = 1'b0;
  assign P4 = 1'b0;
  assign P5 = 1'b0;
  assign P6 = 1'b0;
  assign P7 = 1'b0;
  assign P8 = 1'b0;
endmodule
