// Digital circuit instdecoder.dig as structural Verilog
module instdecoder (
  input  [2:0] fmt,
  input  [1:0] op1,
  input  [3:0] op2,
  input  [4:0] op3,
  output [4:0] op,
  output tworeg,
  output sys
);

  wire rr;

  Decoder #(.Selector_Bits(3)) decoder_1 (
    .sel(fmt), .out_0(sys), .out_2(rr));  // open: out_1, out_3, out_4, out_5, out_6, out_7
  buf or_1 (tworeg, rr);  // Or open: In_2
  Multiplexer #(.Bits(5), .Selector_Bits(3)) multiplexer_1 (
    .sel(fmt), .in_2(op3));  // open: in_0, in_1, in_3, in_4, in_5, in_6, in_7, out
endmodule
