// Digital circuit reg-file.dig as structural Verilog
module reg_file (
  input  [1:0] RS,
  input  [1:0] rd,
  input  [15:0] result,
  input  clock,
  output [15:0] rsval,
  output [15:0] rdval,
  output [15:0] R0,
  output [15:0] R1,
  output [15:0] R2,
  output [15:0] R3
);

  wire decoder_1_out_0, decoder_1_out_1, decoder_1_out_2, decoder_1_out_3;
  wire [15:0] demultiplexer_1_out_0, demultiplexer_1_out_1, demultiplexer_1_out_2, demultiplexer_1_out_3;

  Demultiplexer #(.Selector_Bits(2), .Bits(16)) demultiplexer_1 (
    .sel(rd), .in(result), .out_0(demultiplexer_1_out_0), .out_1(demultiplexer_1_out_1),
    .out_2(demultiplexer_1_out_2), .out_3(demultiplexer_1_out_3));
  Decoder #(.Selector_Bits(2)) decoder_1 (
    .sel(rd), .out_0(decoder_1_out_0), .out_1(decoder_1_out_1), .out_2(decoder_1_out_2),
    .out_3(decoder_1_out_3));
  Register #(.Bits(16)) register_1 (.D(demultiplexer_1_out_0), .C(clock), .en(decoder_1_out_0), .Q(R0));
  Register #(.Bits(16)) register_2 (.D(demultiplexer_1_out_1), .C(clock), .en(decoder_1_out_1), .Q(R1));
  Register #(.Bits(16)) register_3 (.D(demultiplexer_1_out_2), .C(clock), .en(decoder_1_out_2), .Q(R2));
  Register #(.Bits(16)) register_4 (.D(demultiplexer_1_out_3), .C(clock), .en(decoder_1_out_3), .Q(R3));
  Multiplexer #(.Selector_Bits(2), .Bits(16)) multiplexer_1 (
    .sel(RS), .in_0(R0), .in_1(R1), .in_2(R2), .in_3(R3), .out(rsval));
  Multiplexer #(.Selector_Bits(2), .Bits(16)) multiplexer_2 (
    .sel(rd), .in_0(R0), .in_1(R1), .in_2(R2), .in_3(R3), .out(rdval));

  // Notes on the sheet:
  //   RS: default 1
endmodule
