// Digital circuit test.dig as structural Verilog
module test (
  input  clock,
  output halt,
  output error
);

  CPU cpu_1 ();  // open: r0, r1, r2, r3, rd, rd_2, L, rs, target, PC, R, rd_3, rs_2, R_2, halt, error
endmodule

/* Test case add:
clock error halt

# #include "../cpudef.asm"
# 
# move r1, 5
# move r2, 3 
# add r1, r2
# add r1, 2 
# musteq r1, 10

program(0x051c, 0x032c, 0x0091, 0x0210, 0x0a1a)

let i = 0;
while(!(halt | error | (i >= 100)))
  let i = i + 1;
  0 0 0
  1 x x
end while
0 0 1
*/
